// Digital circuit s2p-74HC595.dig as structural Verilog
module s2p_74HC595 (
  input  in_1,
  input  clk,
  output QH,
  output QG,
  output QF,
  output QE,
  output QD,
  output QC,
  output QB,
  output QA
);

  D_FF_AS shift_A (.Set(1'b0), .D(in_1), .C(clk), .Clr(~1'b1), .Q(QA));  // open: nQ
  D_FF_AS shift_B (.Set(1'b0), .D(QA), .C(clk), .Clr(~1'b1), .Q(QB));  // open: nQ
  D_FF_AS shift_C (.Set(1'b0), .D(QB), .C(clk), .Clr(~1'b1), .Q(QC));  // open: nQ
  D_FF_AS shift_D (.Set(1'b0), .D(QC), .C(clk), .Clr(~1'b1), .Q(QD));  // open: nQ
  D_FF_AS shift_E (.Set(1'b0), .D(QD), .C(clk), .Clr(~1'b1), .Q(QE));  // open: nQ
  D_FF_AS shift_F (.Set(1'b0), .D(QE), .C(clk), .Clr(~1'b1), .Q(QF));  // open: nQ
  D_FF_AS shift_G (.Set(1'b0), .D(QF), .C(clk), .Clr(~1'b1), .Q(QG));  // open: nQ
  D_FF_AS shift_H (.Set(1'b0), .D(QG), .C(clk), .Clr(~1'b1), .Q(QH));  // open: nQ
endmodule
